# Fritzing sketch Diseño Programador de Riego (saved by Fritzing 1.0.3b)
breadboards: 2

parts:
  U1 = LM2596 step down module
  Componente1 = Arduino Nano (Rev3.0)
  Part1 = KY-023 Dual Axis Joystick Module [package="Breakout board"]
  GLCD_128x1 = 128 x 64 Graphic LCD
  Part2 = KY-019 5V Relay Module [package="Breakout board"]
  M1 = DC Motor [voltage_(max)=6V voltage_(min)=3V]
  ZS-042_RTC1 = ZS-042 RTC Module
  D1 = bridge rectifier round [package="round [THT]"]
  C1 = Electrolytic Capacitor [capacitance=100µF package="200 mil [THT, electrolytic]"]
  C2 = Tantalum Capacitor [capacitance=1μF package="200 mil [THT, tantalum]"]

nets:
  N1: U1.IN+, D1.DC+, C1.+, C2.+
  GND: U1.IN-, U1.OUT-, Componente1.GND, Part1.GND, GLCD_128x1.2_Vdd, Part2.S, ZS-042_RTC1.GND, D1.DC-, C2.-
  N2: U1.OUT+, Componente1.VIN
  N3: Componente1.D2, GLCD_128x1.20_K(-)
  N4: Componente1.D3, GLCD_128x1.18_Vout
  N5: Componente1.D4, GLCD_128x1.16_CS2
  N6: Componente1.D5, GLCD_128x1.14_DB7
  N7: Componente1.D6, GLCD_128x1.12_DB5
  N8: Componente1.D7, GLCD_128x1.10_DB3
  N9: Componente1.D10, Part1.SW
  N10: Componente1.D11/MOSI, Part2.-
  5V: Componente1.5V, Part1.+5V, GLCD_128x1.4_D/I, Part2.+, ZS-042_RTC1.VCC
  N11: Componente1.A7, Part1.VRy
  N12: Componente1.A6, Part1.VRx
  N13: Componente1.A5, ZS-042_RTC1.SCL
  N14: Componente1.A4, ZS-042_RTC1.SDA
  N15: Part2.Common, M1.pin_1
  N16: Part2.NO, D1.AC#0
  N17: M1.pin_2, D1.AC#1

notes:
  D2 D3 D4 D5 D6 D7 D0 D1 5V GND
  RST
  CS
  RS
  WR
  RD
  24 VAC

custom parts:
  LM2596 step down module: LM2596 DC-DC step down power supply module 3 A.
  KY-019 5V Relay Module: KY-019 5V Relay module, used to control AC circuits.
